# Fritzing sketch SUperMaquina (saved by Fritzing 0.9.3b)
circuit board: 8.46667cm x 5.64444cm
breadboards: 1

parts:
  LED1 = LED - 5mm [color="Red (633nm)" package="5 mm [THT]"]
  Componente1 = Arduino Uno (Rev3)
  R2 = Resistor [tolerance=±5% resistance=330 package=THT]

nets:
  N1: LED1.cathode, Componente1.GND, R2.Pin_0, R2.Pin_1
  N2: LED1.anode, Componente1.D13/SCK

// code stored in the sketch: Superm_quina_-__teste.ino
/**
   sequencial de LEDs ( efeito supermáquina)
   @author - Rogério
*/

void setup() {
  pinMode(13, OUTPUT);

}

void loop() {
  digitalWrite(13, HIGH);
}
